// Logisim project FPA.circ as structural Verilog: 2 circuits, main circuit main
module main (
  input  [31:0] A,
  input  [31:0] B,
  output OverFlow,
  output UnderFlow,
  output [8:0] Larger_Exponent,
  output [31:0] Output
);

  wire inputhandler_1_larger_sign, inputhandler_1_smaller_sign, main_1_outputsign;
  wire [8:0] Normalizer_normalizedexponent, R_Nrm_normalized_exponent;
  wire [31:0] inputhandler_1_larger_fraction, inputhandler_1_shifted_small_fraction,
       main_1_output_of_whole_adder, main_2_rounded_significant, Normalizer_normalizedsignificand,
       R_Nrm_normalized_significand;

  InputHandler inputhandler_1 (
    .InputA(A), .InputB(B), .Exponant_Difference(Larger_Exponent),
    .Larger_Fraction(inputhandler_1_larger_fraction), .Larger_Sign(inputhandler_1_larger_sign),
    .Shifted_Small_Fraction(inputhandler_1_shifted_small_fraction), .Smaller_sign(inputhandler_1_smaller_sign));  // open: out_5, Larger_Exponant, Samller_Fraction
  Adder_main main_1 (
    .A(inputhandler_1_larger_fraction), .B(inputhandler_1_shifted_small_fraction),
    .SIGNA(inputhandler_1_larger_sign), .SIGNB(inputhandler_1_smaller_sign),
    .OUTPUT_OF_WHOLE_ADDER(main_1_output_of_whole_adder), .OUTPUTSIGN(main_1_outputsign));  // open: out_5
  Normalizer_main Normalizer (
    .Exponent_Input(Larger_Exponent), .Significand_Input(main_1_output_of_whole_adder),
    .UnderFlow(UnderFlow), .OverFlow(OverFlow), .NormalizedExponent(Normalizer_normalizedexponent),
    .NormalizedSignificand(Normalizer_normalizedsignificand));  // open: Denormalized
  Rounder_main main_2 (.in_1(Normalizer_normalizedsignificand), .ROUNDED_SIGNIFICANT(main_2_rounded_significant));
  Rounded_Normalizer R_Nrm (
    .Exponent_Input(Normalizer_normalizedexponent), .Significand_Input(main_2_rounded_significant),
    .Normalized_Exponent(R_Nrm_normalized_exponent), .Normalized_Significand(R_Nrm_normalized_significand));  // open: Overflow
  Output_Handler OpH (
    .Significand(R_Nrm_normalized_significand[29:8]), .Exponent(R_Nrm_normalized_exponent),
    .Sign(main_1_outputsign), .Output(Output));
endmodule

module Output_Handler (
  input  [21:0] Significand,
  input  [8:0] Exponent,
  input  Sign,
  output [31:0] Output
);


  assign Output = {Sign, Exponent, Significand};
endmodule
